// Logisim project main.circ as structural Verilog: 2 circuits, main circuit main
module main (
);

  wire CLC;
  wire [3:0] ALU_OP;
  wire [15:0] ALU_out, PC_q, R1_q, R2_q, ram_1_data;
  wire [23:4] Program_data;

  Clock clock_1 (.out(CLC));
  Counter #(.width(16), .max('hffff), .ongoal("stay")) PC (
    .Q(PC_q), .clk(CLC));  // open: load, D, count, carry, clr, preset, down
  ROM #(.addrWidth(16), .dataWidth(24), .Select("low")) Program (.addr(PC_q), .data({Program_data, ALU_OP}));
  RAM #(.addrWidth(16), .dataWidth(16), .Select("low")) ram_1 (
    .addr(PC_q), .data(ram_1_data), .clk(CLC));  // open: sel, ld, clr
  Register #(.width(16), .Select("low")) R1 (.D(ALU_out), .en(1'b1), .Q(R1_q), .clk(CLC));  // open: clr
  Register #(.width(16), .Select("low")) R2 (.en(1'b1), .Q(R2_q), .clk(CLC));  // open: D, clr
  alu ALU (.A(R1_q), .B(R2_q), .ALU_OP(ALU_OP), .OUT(ALU_out));  // open: IN_FLAGS, OUT_FLAGS

  // Notes on the sheet:
  //   Main architecture
endmodule

module alu (
  input  [15:0] A,
  input  [15:0] B,
  input  [3:0] ALU_OP,
  input  [3:0] IN_FLAGS,
  output [15:0] OUT,
  output [3:0] OUT_FLAGS
);

  wire [15:0] adder_1_out;

  Adder #(.width(16)) adder_1 (.a(A), .b(B), .out(adder_1_out), .cin(IN_FLAGS[0]));  // open: cout
  Multiplexer #(.select(4), .width(16), .enable("false")) multiplexer_1 (
    .in0(adder_1_out), .out(OUT), .sel(ALU_OP));  // open: in1, in2, in3, in4, in5, in6, in7, in8, in9, in10, in11, in12, in13, in14, in15

  // Notes on the sheet:
  //   ALU interface
endmodule
